// Digital circuit 74779.dig as structural Verilog
// 8-Bit Bidirectional Binary Counter with 3-STATE Outputs
module _74779 (
  input  CP,
  input  S0,
  input  S1,
  input  nOE,
  input  I_O0,
  input  I_O1,
  input  I_O2,
  input  I_O3,
  input  I_O4,
  input  I_O5,
  input  I_O6,
  input  I_O7,
  input  nCET,
  input  VCC,
  input  GND,
  output nTC,
  output I_O0_outx,
  output I_O1_outx,
  output I_O2_outx,
  output I_O3_outx,
  output I_O4_outx,
  output I_O5_outx,
  output I_O6_outx,
  output I_O7_outx
);

  wire _74779_inc_1_p5, _74779_inc_1_p6, _74779_inc_2_p5, _74779_inc_2_p6, _74779_inc_3_p5, _74779_inc_3_p6,
       _74779_inc_4_p5, _74779_inc_4_p6, _74779_inc_5_p5, _74779_inc_5_p6, _74779_inc_6_p5, _74779_inc_6_p6,
       _74779_inc_7_p5, _74779_inc_7_p6, _74779_inc_8_p5, _74779_inc_8_p6, and_1_out, and_2_out, and_3_out,
       and_4_out, and_5_out, and_6_out, and_7_out, and_8_out, and_9_out, and_10_out, and_11_out, and_12_out,
       and_13_out, and_14_out, and_15_out, and_16_out, and_17_out, and_18_out, and_19_out, and_20_out,
       and_21_out, and_22_out, and_23_out, and_24_out, and_25_out, and_26_out, and_27_out, and_28_out,
       and_29_out, and_30_out, and_31_out, and_32_out, and_33_out, and_34_out, and_35_out, and_36_out,
       and_37_out, and_38_out, and_39_out, nor_2_out, nor_3_out, nor_4_out, nor_5_out, nor_6_out, nor_7_out,
       nor_8_out, not_1_out, not_2_out, not_3_out, not_4_out, not_5_out, not_6_out, not_7_out, not_8_out,
       not_9_out, not_10_out, not_11_out, not_12_out, not_13_out, not_14_out, not_15_out;

  not not_1 (not_1_out, S0);
  not not_2 (not_2_out, S1);
  not not_3 (not_3_out, nOE);
  not not_4 (not_4_out, not_2_out);
  not not_5 (not_5_out, not_1_out);
  assign I_O0_outx = not_3_out ? not_7_out : 1'bz;  // Driver driver_1
  assign I_O1_outx = not_3_out ? not_8_out : 1'bz;  // Driver driver_2
  assign I_O2_outx = not_3_out ? not_9_out : 1'bz;  // Driver driver_3
  assign I_O3_outx = not_3_out ? not_10_out : 1'bz;  // Driver driver_4
  assign I_O4_outx = not_3_out ? not_11_out : 1'bz;  // Driver driver_5
  assign I_O5_outx = not_3_out ? not_12_out : 1'bz;  // Driver driver_6
  assign I_O6_outx = not_3_out ? not_13_out : 1'bz;  // Driver driver_7
  assign I_O7_outx = not_3_out ? not_14_out : 1'bz;  // Driver driver_8
  not not_6 (not_6_out, nCET);
  and and_1 (and_1_out, not_1_out, not_2_out);
  and and_2 (and_2_out, not_4_out, not_1_out);
  and and_3 (and_3_out, not_2_out, not_5_out);
  not not_7 (not_7_out, _74779_inc_1_p6);
  not not_8 (not_8_out, _74779_inc_2_p6);
  not not_9 (not_9_out, _74779_inc_3_p6);
  not not_10 (not_10_out, _74779_inc_4_p6);
  not not_11 (not_11_out, _74779_inc_5_p6);
  not not_12 (not_12_out, _74779_inc_6_p6);
  not not_13 (not_13_out, _74779_inc_7_p6);
  not not_14 (not_14_out, _74779_inc_8_p6);
  and and_4 (and_4_out, _74779_inc_3_p6, _74779_inc_2_p6, _74779_inc_1_p6, and_3_out, not_6_out);
  and and_5 (and_5_out, and_7_out, and_4_out);
  and and_6 (and_6_out, _74779_inc_1_p6, and_3_out, not_6_out);
  and and_7 (and_7_out, _74779_inc_8_p6, _74779_inc_7_p6, _74779_inc_6_p6, _74779_inc_5_p6, _74779_inc_4_p6);
  and and_8 (and_8_out, _74779_inc_2_p6, _74779_inc_1_p6, and_3_out, not_6_out);
  and and_9 (and_9_out, _74779_inc_3_p6, _74779_inc_2_p6, _74779_inc_1_p6, and_3_out, not_6_out);
  and and_10 (and_10_out, _74779_inc_4_p6, _74779_inc_3_p6, _74779_inc_2_p6);
  and and_11 (and_11_out, _74779_inc_1_p6, and_3_out, not_6_out);
  and and_12 (and_12_out, _74779_inc_5_p6, _74779_inc_4_p6, _74779_inc_3_p6);
  and and_13 (and_13_out, _74779_inc_2_p6, _74779_inc_1_p6, and_3_out, not_6_out);
  and and_14 (and_14_out, _74779_inc_6_p6, _74779_inc_5_p6, _74779_inc_4_p6, _74779_inc_3_p6);
  and and_15 (and_15_out, _74779_inc_2_p6, _74779_inc_1_p6, and_3_out, not_6_out);
  and and_16 (and_16_out, _74779_inc_7_p6, _74779_inc_6_p6, _74779_inc_5_p6, _74779_inc_4_p6);
  and and_17 (and_17_out, _74779_inc_3_p6, _74779_inc_2_p6, _74779_inc_1_p6, and_3_out, not_6_out);
  and and_18 (and_18_out, and_10_out, and_11_out);
  and and_19 (and_19_out, and_12_out, and_13_out);
  and and_20 (and_20_out, and_14_out, and_15_out);
  and and_21 (and_21_out, and_16_out, and_17_out);
  and and_22 (and_22_out, _74779_inc_3_p5, _74779_inc_2_p5, _74779_inc_1_p5, and_2_out, not_6_out);
  and and_23 (and_23_out, and_24_out, and_22_out);
  and and_24 (and_24_out, _74779_inc_8_p5, _74779_inc_7_p5, _74779_inc_6_p5, _74779_inc_5_p5, _74779_inc_4_p5);
  and and_25 (and_25_out, not_6_out, _74779_inc_1_p5, and_2_out);
  and and_26 (and_26_out, not_6_out, _74779_inc_2_p5, _74779_inc_1_p5, and_2_out);
  nor nor_1 (nTC, and_23_out, and_5_out);
  PowerSupply powersupply_1 (.VDD(VCC), .GND(GND));
  and and_27 (and_27_out, not_6_out, _74779_inc_3_p5, _74779_inc_2_p5, _74779_inc_1_p5, and_2_out);
  and and_28 (and_28_out, not_6_out, _74779_inc_4_p5, _74779_inc_3_p5);
  and and_29 (and_29_out, _74779_inc_2_p5, _74779_inc_1_p5, and_2_out);
  and and_30 (and_30_out, not_6_out, _74779_inc_5_p5, _74779_inc_4_p5);
  and and_31 (and_31_out, _74779_inc_3_p5, _74779_inc_2_p5, _74779_inc_1_p5, and_2_out);
  and and_32 (and_32_out, not_6_out, _74779_inc_6_p5, _74779_inc_5_p5, _74779_inc_4_p5);
  and and_33 (and_33_out, _74779_inc_3_p5, _74779_inc_2_p5, _74779_inc_1_p5, and_2_out);
  and and_34 (and_34_out, not_6_out, _74779_inc_7_p5, _74779_inc_6_p5, _74779_inc_5_p5);
  and and_35 (and_35_out, _74779_inc_4_p5, _74779_inc_3_p5, _74779_inc_2_p5, _74779_inc_1_p5, and_2_out);
  and and_36 (and_36_out, and_28_out, and_29_out);
  and and_37 (and_37_out, and_30_out, and_31_out);
  and and_38 (and_38_out, and_32_out, and_33_out);
  and and_39 (and_39_out, and_34_out, and_35_out);
  not not_15 (not_15_out, not_6_out);
  nor nor_2 (nor_2_out, and_25_out, and_6_out);
  nor nor_3 (nor_3_out, and_26_out, and_8_out);
  nor nor_4 (nor_4_out, and_27_out, and_9_out);
  nor nor_5 (nor_5_out, and_36_out, and_18_out);
  nor nor_6 (nor_6_out, and_37_out, and_19_out);
  nor nor_7 (nor_7_out, and_38_out, and_20_out);
  nor nor_8 (nor_8_out, and_39_out, and_21_out);
  // _74779_inc _74779_inc_1: pin names not known; wires that end beside it: I_O0, and_1_out, not_15_out, CP, _74779_inc_1_p5, _74779_inc_1_p6
  // _74779_inc _74779_inc_2: pin names not known; wires that end beside it: I_O1, and_1_out, nor_2_out, CP, _74779_inc_2_p5, _74779_inc_2_p6
  // _74779_inc _74779_inc_3: pin names not known; wires that end beside it: I_O2, and_1_out, nor_3_out, CP, _74779_inc_3_p5, _74779_inc_3_p6
  // _74779_inc _74779_inc_4: pin names not known; wires that end beside it: I_O3, and_1_out, nor_4_out, CP, _74779_inc_4_p5, _74779_inc_4_p6
  // _74779_inc _74779_inc_5: pin names not known; wires that end beside it: I_O4, and_1_out, nor_5_out, CP, _74779_inc_5_p5, _74779_inc_5_p6
  // _74779_inc _74779_inc_6: pin names not known; wires that end beside it: I_O5, and_1_out, nor_6_out, CP, _74779_inc_6_p5, _74779_inc_6_p6
  // _74779_inc _74779_inc_7: pin names not known; wires that end beside it: I_O6, and_1_out, nor_7_out, CP, _74779_inc_7_p5, _74779_inc_7_p6
  // _74779_inc _74779_inc_8: pin names not known; wires that end beside it: I_O7, and_1_out, nor_8_out, CP, _74779_inc_8_p5, _74779_inc_8_p6

  // Notes on the sheet:
  //   CP: pin 15
  //   S0: pin 11
  //   S1: pin 10
  //   nOE: pin 9, default 1
  //   I_O0: pin 16
  //   I_O1: pin 1
  //   I_O2: pin 2
  //   I_O3: pin 3
  //   I_O4: pin 5
  //   I_O5: pin 6
  //   I_O6: pin 7
  //   I_O7: pin 8
  //   nCET: pin 14, default 1
  //   nTC: pin 12
  //   VCC: pin 13, default 1
  //   GND: pin 4
endmodule

/* Test case:
S1 S0 ~CET ~OE CP I/O7 I/O6 I/O5 I/O4 I/O3 I/O2 I/O1 I/O0 I/O7_out I/O6_out I/O5_out I/O4_out I/O3_out I/O2_out I/O1_out I/O0_out ~TC
0  0    0   1   C  bits(8,1)          bits(8,1) 1
x  x    x   1   0  Z Z Z Z Z Z Z Z    Z Z Z Z Z Z Z Z 1
loop(n,256)
0  0    0   1   C  bits(8,n)          bits(8,n) 1
0  0    0   0   0  Z Z Z Z Z Z Z Z    bits(8,n) 1
0  0    1   1   C  bits(8,n)          bits(8,n) 1
0  0    1   0   0  Z Z Z Z Z Z Z Z    bits(8,n) 1

1  0    1   0   C  Z Z Z Z Z Z Z Z    bits(8,n) 1
0  1    1   0   C  Z Z Z Z Z Z Z Z    bits(8,n) 1
1  1    1   0   C  Z Z Z Z Z Z Z Z    bits(8,n) 1
end loop

loop(n,255)
1  0    0   0   C  Z Z Z Z Z Z Z Z    bits(8,n) 1
end loop
1  0    0   0   C  Z Z Z Z Z Z Z Z    bits(8,-1) 0

loop(n,254)
0  1    0   0   C  Z Z Z Z Z Z Z Z    bits(8,254-n) 1
end loop
0  1    0   0   C  Z Z Z Z Z Z Z Z    bits(8,0) 0
*/
