// Digital circuit adder.dig as structural Verilog
module adder (
  input  [7:0] A,
  input  [7:0] B,
  output [7:0] S,
  output C
);

  Add #(.Bits(8)) add_1 (.a(A), .b(B), .c_i(1'b0), .s(S), .c_o(C));
endmodule

/* Test case Simple:
A B |S| C
1 1 2 X
*/

/* Test case Failing:
A B |S| C
1 1 3 X
*/
