// Digital circuit test.dig as structural Verilog
module test (
  input  [7:0] A,
  input  [7:0] B,
  output [7:0] S,
  output C
);

  Add #(.Bits(8)) add_1 (.a(A), .b(B), .c_i(1'b0), .s(S), .c_o(C));
endmodule

/* Test case:
A    B    S    C

1    1    2    0
0xFF 0x01 0x00 1

loop (a,256)
loop (b,256)
(a)  (b)  (a+b) ((a+b) > 0xFF)
end loop
end loop
*/

/* Test case Simple:
A B S C
1 1 2 X
*/
